# Fritzing sketch Circuito integrado (saved by Fritzing 0.9.7b)
circuit board: 5cm x 5.5cm
breadboards: 1

parts:
  Q1 = PNP-Transistor [package="TO92 [THT]"]
  R1 = Resistor [tolerance=±5% power=0.25 resistance=100k package=THT]
  R2 = Resistor [tolerance=±5% power=0.25 resistance=3.3k package=THT]
  R3 = Resistor [tolerance=±5% power=0.25 resistance=8.2k package=THT]
  C3 = Ceramic Capacitor [capacitance=0.1µF voltage=35V package="100 mil [THT, multilayer]"]
  Q2 = PNP-Transistor [package="TO92 [THT]"]
  C2 = Tantalum Capacitor [capacitance=1µF voltage=35V package="100 mil [THT, tantalum]"]
  BAT1 = BC9VPC [package=bc9vpc]
  C1 = Electrolytic Capacitor [capacitance=2.2µF voltage=50V package="100 mil [THT, electrolytic]"]
  JInput = 1/4 inch mono jack [package=audio-jack-6.5mm-panel-mount]
  RVolumen = Trimmer Potentiometer [maximum_resistance=500k package=THT]
  LED1 = LED - 3mm [color="Red (633nm)" current=0.030 package="3 mm [THT]"]
  RTono = Trimmer Potentiometer [maximum_resistance=1kΩ package=THT]
  JOutput = 1/4 inch mono jack [package=audio-jack-6.5mm-panel-mount]
  R4 = Resistor [tolerance=±5% power=0.25 resistance=470 package=THT]
  S1 = SWITCH-3PDT [package=ms]

nets:
  GND: Q1.E, C2.+, BAT1.V+, JInput.Sleeve, RVolumen.leg1, LED1.anode, RTono.leg2, JOutput.Sleeve
  N1: Q1.B, R1.Pin_1, C1.-
  N2: Q1.C, R2.Pin_0, Q2.B
  N3: R1.Pin_0, Q2.E, RTono.leg1
  N4: R2.Pin_1, BAT1.V-, R4.Pin_0, S1.3
  N5: R3.Pin_0, Q2.C
  N6: R3.Pin_1, C3.0, R4.Pin_1
  N7: C3.1, RVolumen.leg2
  N8: C2.-, RTono.wiper
  N9: C1.+, S1.1
  N10: JInput.Tip, S1.4
  N11: RVolumen.wiper, S1.5
  N12: LED1.cathode, S1.6
  N13: JOutput.Tip, S1.2, S1.pin_7

notes:
  BRJ Design

custom parts:
  1/4 inch mono jack: 1/4 inch mono Audio Jack Simple 1/4 inch panel mount audio jack.
  SWITCH-3PDT: 3PDT Stomp Switch
